# Fritzing sketch wiring_diagram (saved by Fritzing 0.9.2b)

parts:
  Bauteil1 = Arduino Uno (Rev3)
  Bauteil2 = SeeedStudio Can-Bus Shield
  J1 = shrouded pin header, 32 pins [form="♂ (shrouded male)"]
  R1 = Trimmer Potentiometer [maximum_resistance=200 package=THT]
  R2 = Trimmer Potentiometer [maximum_resistance=10kΩ package=THT]
  U1 = LCD-16X2 [package=lcd-16x2_noholes]
  LCM1602_IIC1 = LCM1602 IIC [part_number="LCM1602 IIC" chip_label="LCM1602 IIC" package="DIP (Dual Inline) [THT]"]
  LED5 = LED - 5mm [color="Green (565nm)" package="5 mm [THT]"]
  LED7 = LED - 5mm [color="Orange (612nm)" package="5 mm [THT]"]
  LED8 = LED - 5mm [color="Red (633nm)" package="5 mm [THT]"]
  LED6 = LED - 5mm [color="Green (565nm)" package="5 mm [THT]"]

nets:
  N1: Bauteil1.A0, LED5.cathode
  N2: Bauteil1.A1, LED6.cathode
  N3: Bauteil1.A2, LED8.cathode
  N4: Bauteil1.A3, LED7.cathode
  N5: Bauteil1.A4/SDA, LCM1602_IIC1.SDA
  N6: Bauteil1.A5/SCL, LCM1602_IIC1.SCL
  GND: Bauteil1.GND, J1.pin17, R1.wiper, LCM1602_IIC1.GND, LED5.anode, LED7.anode, LED8.anode, LED6.anode
  N7: Bauteil1.5V, J1.pin1, J1.pin2, J1.pin18
  N8: Bauteil1.VIN, J1.pin15, J1.pin16
  5V: Bauteil2.5V, J1.pin10, LCM1602_IIC1.VCC
  N9: Bauteil2.GND, J1.pin4, J1.pin6, J1.pin12, R2.wiper
  N10: Bauteil2.CANH, J1.pin13
  N11: Bauteil2.CANL, J1.pin14
  N12: Bauteil2.MOSI, J1.pin9, J1.pin11
  N13: Bauteil2.MISO, J1.pin20
  N14: Bauteil2.SCK, J1.pin19
  N15: J1.pin3, J1.pin5, R2.leg1
  N16: J1.pin29, J1.pin31, R1.leg2
  N17: J1.pin32, R1.leg1
  VSS: U1.VSS, LCM1602_IIC1.VSS
  VDD: U1.VDD, LCM1602_IIC1.VDD
  N18: U1.VO, LCM1602_IIC1.V0
  N19: U1.RS, LCM1602_IIC1.RS
  N20: U1.R_W, LCM1602_IIC1.RW
  N21: U1.E, LCM1602_IIC1.E
  N22: U1.DB0, LCM1602_IIC1.D0
  N23: U1.DB1, LCM1602_IIC1.D1
  N24: U1.DB2, LCM1602_IIC1.D2
  N25: U1.DB3, LCM1602_IIC1.D3
  N26: U1.DB4, LCM1602_IIC1.D4
  N27: U1.DB5, LCM1602_IIC1.D5
  N28: U1.DB6, LCM1602_IIC1.D6
  N29: U1.DB7, LCM1602_IIC1.D7
  N30: U1.A, LCM1602_IIC1.A
  N31: U1.K, LCM1602_IIC1.K

notes:
  1
  16
  17
  32
  20kOhm
  200 Ohm
  Vin = 12V
  External Power Supply

custom parts:
  SeeedStudio Can-Bus Shield: This CAN-BUS Shield adopts MCP2515 CAN Bus controller with SPI interface and MCP2551 CAN transceiver to give your Arduino/Seeeduino CAN-BUS capibility. With an OBD-II converter cable added on and the OBD-II library imported, you are ready to build an onboard diagnostic device or data logger. Features Implements CAN V2.0B at up to 1 Mb/s SPI Interface up to 10 MHz Standard (11 bit) and extended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
  LCM1602 IIC: I2C-Module to use a 1602 or 2004 LCD on with the wire.h libory Serial LCD Modul
